# Fritzing sketch giris_sistemi (saved by Fritzing 1.0.2b)
breadboards: 1

parts:
  Driver1 = 28BYJ-48 Driver Module [part_number=ULN2003 package=THT]
  SM1 = 28BYJ-48 Stepper Motor [part_number=28BYJ-48]  # not connected
  Parça1 = RFID-RC522-v2
  Deneyap_Kart1 = Deneyap Kart Deneyap 1A [package="DIP (Dual Inline) [THT]"]
  LED1 = LED - 5mm [color="Red (633nm)" current=0.030A package="5 mm [THT]"]
  LED2 = LED - 5mm [color="Green (560nm)" current=0.030A package="5 mm [THT]"]
  J1 = Piezo Speaker

nets:
  N1: Driver1.IN1, Deneyap_Kart1.D1
  N2: Driver1.IN2, Deneyap_Kart1.D4
  N3: Driver1.IN3, Deneyap_Kart1.D12
  N4: Driver1.IN4, Deneyap_Kart1.D9
  N5: Parça1.SDA, Deneyap_Kart1.SDA
  N6: Parça1.SCK, Deneyap_Kart1.SCK
  N7: Parça1.MOSI, Deneyap_Kart1.MOSI
  N8: Parça1.MISO, Deneyap_Kart1.MISO
  N9: Parça1.GND, Deneyap_Kart1.GND#15, LED1.cathode, LED2.cathode, J1.pin1
  N10: Parça1.RST, Deneyap_Kart1.D0
  N11: Parça1.3.3V, Deneyap_Kart1.3V3#17
  N12: Deneyap_Kart1.D15, LED1.anode
  N13: Deneyap_Kart1.D14, LED2.anode
  N14: Deneyap_Kart1.D13, J1.pin2

custom parts:
  28BYJ-48 Driver Module: Generic male header
  28BYJ-48 Stepper Motor: Unipolar Stepper Motor 28BYJ-48 Top coil - pink & orange Bottom coil - blue & yellow Common rail - red Connector pins: blue - pink - yellow - orange - red
  RFID-RC522-v2: A simple China made RFID-RC522 Reader; do check the pin labels, as this is a MFRC522 based clone.
  Deneyap Kart Deneyap 1A: Ülkemizin mühendislik kaynakları kullanılarak geliştirilen Deneyap Kart Deneyap 1A; güçlü işlemcisi, dayanıklı tasarımı ve çok yönlü giriş/çıkış pinleri ile kullanıcılara Elektronik Programlama, Nesnelerin İnterneti (IoT) ve Yapay Zeka alanlarında başlangıç seviyesinden endüstriyel uygulamalara kadar her seviyede projeyi yapma imkanı sunuyor.
